// Digital circuit 01.dig as structural Verilog
module _01 (
  input  A,
  input  B,
  input  C,
  input  D,
  input  A_2,
  output [3:0] Z
);

  Seven_Seg_Hex seven_seg_hex_1 (.d({D, C, B, A}), .dp(A_2));

  assign Z = {D, C, B, A};
endmodule
