// Digital circuit 2421.dig as structural Verilog
module _2421 (
  input  [3:0] A,
  output [3:0] Z
);

  wire and_1_out, and_2_out, and_3_out, and_4_out, and_5_out, and_6_out, not_1_out, not_2_out, not_3_out;

  not not_1 (not_1_out, A[2]);
  not not_2 (not_2_out, A[1]);
  not not_3 (not_3_out, A[0]);
  and and_1 (and_1_out, A[2], not_2_out, A[0]);
  and and_2 (and_2_out, A[2], A[1]);
  and and_3 (and_3_out, A[2], not_3_out);
  and and_4 (and_4_out, A[2], A[1]);
  and and_5 (and_5_out, not_1_out, A[1]);
  and and_6 (and_6_out, A[2], not_2_out, A[0]);
  or or_1 (Z[3], A[3], and_1_out, and_2_out);
  or or_2 (Z[2], A[3], and_3_out, and_4_out);
  or or_3 (Z[1], A[3], and_5_out, and_6_out);

  assign Z[0] = A[0];
endmodule
