// Digital circuit Excess3.dig as structural Verilog
module Excess3 (
  input  [3:0] A,
  output [3:0] Z
);

  wire and_1_out, and_2_out, and_3_out, and_4_out, and_5_out, and_6_out, and_7_out, and_8_out, and_9_out,
       and_10_out, not_1_out, not_2_out, not_3_out;

  not not_1 (not_1_out, A[2]);
  not not_2 (not_2_out, A[1]);
  not not_3 (not_3_out, A[0]);
  and and_1 (and_1_out, A[2], A[1], not_3_out);
  and and_2 (and_2_out, A[2], A[0]);
  and and_3 (and_3_out, A[2], not_2_out, not_3_out);
  and and_4 (and_4_out, not_1_out, A[1], not_3_out);
  and and_5 (and_5_out, not_1_out, A[0]);
  and and_6 (and_6_out, A[1], A[0]);
  and and_7 (and_7_out, not_2_out, not_3_out);
  and and_8 (and_8_out, not_1_out, A[1], not_3_out);
  and and_9 (and_9_out, A[2], A[1], not_3_out);
  and and_10 (and_10_out, not_2_out, not_3_out);
  or or_1 (Z[3], A[3], and_1_out, and_2_out);
  or or_2 (Z[2], and_3_out, and_4_out, and_5_out);
  or or_3 (Z[1], and_6_out, and_7_out);
  or or_4 (Z[0], and_8_out, and_9_out, and_10_out);
endmodule
