// Digital circuit Templatet.dig as structural Verilog
module Templatet (
  input  [3:0] In,
  input  [1:0] Selector,
  output [3:0] Output
);

  wire [3:0] _642_3_1_z, _2421_1_z, cyclic_1_z, excess3_1_z;

  Excess3 excess3_1 (.A(In), .Z(excess3_1_z));
  Cyclic cyclic_1 (.A(In), .Z(cyclic_1_z));
  _2421 _2421_1 (.A(In), .Z(_2421_1_z));
  _642_3 _642_3_1 (.A(In), .Z(_642_3_1_z));
  Multiplexer #(.Bits(4), .Selector_Bits(2)) multiplexer_1 (
    .sel(Selector), .in_0(excess3_1_z), .in_1(cyclic_1_z), .in_2(_2421_1_z), .in_3(_642_3_1_z), .out(Output));
endmodule
