// Digital circuit CSplitter.dig as structural Verilog
module CSplitter (
  input  [6:0] A,
  output C1,
  output C2,
  output C3
);

  xor xor_1 (C1, A[3], A[2], A[1], A[0]);
  xor xor_2 (C2, A[5], A[4], A[1], A[0]);
  xor xor_3 (C3, A[6], A[4], A[2], A[0]);
endmodule
