// Digital circuit Corrector.dig as structural Verilog
module Corrector (
  input  C1,
  input  C2,
  input  C3,
  output [6:0] Z
);

  Multiplexer #(.Selector_Bits(3), .Bits(7)) multiplexer_1 (
    .sel({C1, C2, C3}), .in_0({7{1'b0}}), .in_1(7'b1000000), .in_2(7'b0100000), .in_3(7'b0010000),
    .in_4(7'b0001000), .in_5(7'b0000100), .in_6(7'b0000010), .in_7(7'b0000001), .out(Z));
endmodule
