// Digital circuit Template.dig as structural Verilog
module Template (
  input  [6:0] In,
  output [6:0] Output
);

  wire csplitter_1_c1, csplitter_1_c2, csplitter_1_c3;
  wire [6:0] corrector_1_z;

  CSplitter csplitter_1 (.A(In), .C1(csplitter_1_c1), .C2(csplitter_1_c2), .C3(csplitter_1_c3));
  Corrector corrector_1 (.C1(csplitter_1_c1), .C2(csplitter_1_c2), .C3(csplitter_1_c3), .Z(corrector_1_z));
  assign Output = corrector_1_z ^ In;  // XOr xor_1, 7 bits wide
endmodule
