// Digital circuit PlusOne.dig as structural Verilog
module PlusOne (
  input  [8:0] A,
  output [8:0] Sum
);

  wire halfadder_1_p4, halfadder_2_p4, halfadder_3_p4, halfadder_4_p4, halfadder_5_p4, halfadder_6_p4,
       halfadder_7_p4, halfadder_8_p4;

  // HalfAdder halfadder_1: pin names not known; wires that end beside it: A[0], 1'b1, Sum[0], halfadder_1_p4
  // HalfAdder halfadder_2: pin names not known; wires that end beside it: halfadder_1_p4, A[1], Sum[1], halfadder_2_p4
  // HalfAdder halfadder_3: pin names not known; wires that end beside it: halfadder_2_p4, A[2], Sum[2], halfadder_3_p4
  // HalfAdder halfadder_4: pin names not known; wires that end beside it: halfadder_3_p4, A[3], Sum[3], halfadder_4_p4
  // HalfAdder halfadder_5: pin names not known; wires that end beside it: halfadder_4_p4, A[4], Sum[4], halfadder_5_p4
  // HalfAdder halfadder_6: pin names not known; wires that end beside it: halfadder_5_p4, A[5], Sum[5], halfadder_6_p4
  // HalfAdder halfadder_7: pin names not known; wires that end beside it: halfadder_6_p4, A[6], Sum[6], halfadder_7_p4
  // HalfAdder halfadder_8: pin names not known; wires that end beside it: halfadder_7_p4, A[7], Sum[7], halfadder_8_p4
  // HalfAdder halfadder_9: pin names not known; wires that end beside it: halfadder_8_p4, A[8], Sum[8]
endmodule
