// Digital circuit Template.dig as structural Verilog
module Template (
  input  [7:0] In,
  output [8:0] Output,
  output [8:0] Output2
);

  wire [7:0] xor_1_out;

  assign xor_1_out = In ^ {8{1'b1}};  // XOr xor_1, 8 bits wide
  Add #(.Bits(9)) add_1 (.a({1'b1, xor_1_out}), .b(9'h1), .c_i(1'b0), .s(Output));  // open: c_o
  PlusOne plusone_1 (.A({1'b1, xor_1_out}), .Sum(Output2));
endmodule
