// Digital circuit Template.dig as structural Verilog
module Template (
  input  [3:0] In,
  output [3:0] Out
);

  wire and_1_out, halfadder_1_p4, halfadder_2_p4;
  wire [2:0] halfadder_1_p3, xor_1_out;
  wire [3:0] multiplexer_1_out;

  assign xor_1_out = In[2:0] ^ 3'b111;  // XOr xor_1, 3 bits wide
  // HalfAdder halfadder_1: pin names not known; wires that end beside it: xor_1_out[0], 1'b1, halfadder_1_p3[0], halfadder_1_p4
  and and_1 (and_1_out, xor_1_out[0], xor_1_out[1], xor_1_out[2]);
  // HalfAdder halfadder_2: pin names not known; wires that end beside it: halfadder_1_p4, xor_1_out[1], halfadder_1_p3[1], halfadder_2_p4
  // HalfAdder halfadder_3: pin names not known; wires that end beside it: halfadder_2_p4, xor_1_out[2], halfadder_1_p3[2]
  Multiplexer #(.Bits(4)) multiplexer_1 (
    .sel(and_1_out), .in_0({In[3], halfadder_1_p3}), .in_1(4'b0000), .out(multiplexer_1_out));
  Multiplexer #(.Bits(4)) multiplexer_2 (.sel(In[3]), .in_0(In), .in_1(multiplexer_1_out), .out(Out));
endmodule
