// Digital circuit PlusOne.dig as structural Verilog
module PlusOne (
  input  [3:0] A,
  input  Cin,
  output [3:0] B,
  output Cout
);

  Add #(.Bits(4)) add_1 (.a(A), .b(4'b0001), .c_i(Cin), .s(B), .c_o(Cout));
endmodule
