// Digital circuit Template.dig as structural Verilog
module Template (
  input  [3:0] A,
  input  [3:0] B,
  input  [2:0] S,
  input  M,
  input  C,
  output [3:0] F,
  output Cout
);

  wire add_2_c_o, C1, C2, C3, C4, C5, C6, multiplexer_4_out;
  wire [3:0] A_1, A_1_t, A_and_B, A_and_Bn, A_B_1, A_nand_B, A_nor_B, A_or_B, A_plus_B, A_plus_C, A_xnor_B,
       add_2_s, ALS, An, ARS, B_plus_C, Bn, comp_1_a_2, comp_2_a_2, multiplexer_1_out, multiplexer_2_out;

  assign An = ~A;  // Not not_1, 4 bits wide
  assign Bn = ~B;  // Not not_2, 4 bits wide
  assign A_nand_B = ~(A & B);  // NAnd nand_1, 4 bits wide
  assign A_nor_B = ~(A | B);  // NOr nor_1, 4 bits wide
  assign A_xnor_B = ~(A ^ B);  // XNOr xnor_1, 4 bits wide
  assign A_and_B = A & B;  // And and_1, 4 bits wide
  assign A_or_B = A | B;  // Or or_1, 4 bits wide
  assign A_and_Bn = A & Bn;  // And and_2, 4 bits wide
  Multiplexer #(.Selector_Bits(3), .Bits(4)) multiplexer_1 (
    .sel(S), .in_0(An), .in_1(A_nand_B), .in_2(A_nor_B), .in_3(A_xnor_B), .in_4(A_and_B), .in_5(A_or_B),
    .in_6(A_and_Bn), .in_7(A), .out(multiplexer_1_out));
  Multiplexer #(.Selector_Bits(3), .Bits(4)) multiplexer_2 (
    .sel(S), .in_0(A_plus_C), .in_1(A_1_t), .in_2(A_plus_B), .in_3(A_B_1), .in_4(A_1), .in_5(B_plus_C),
    .in_6(ALS), .in_7(ARS), .out(multiplexer_2_out));
  MinusOne minusone_1 (.A(A), .Cin(C), .B(A_1_t), .Cout(C2));
  Add #(.Bits(4)) add_1 (.a(A), .b(B), .c_i(C), .s(A_plus_B), .c_o(C3));
  Comp comp_1 (.A(B), .A_2(comp_1_a_2));
  Comp comp_2 (.A(A), .A_2(comp_2_a_2));
  LeftShift leftshift_1 (.A(A), .Out(ALS));
  RightShift rightshift_1 (.A(A), .Out(ARS));
  Add #(.Bits(4)) add_2 (.a(A), .b(comp_1_a_2), .c_i(C), .s(add_2_s), .c_o(add_2_c_o));
  MinusOne minusone_2 (.A(comp_2_a_2), .Cin(C), .B(A_1), .Cout(C5));
  MinusOne minusone_3 (.A(add_2_s), .Cin(add_2_c_o), .B(A_B_1), .Cout(C4));
  Multiplexer #(.Bits(4)) multiplexer_3 (.sel(M), .in_0(multiplexer_1_out), .in_1(multiplexer_2_out), .out(F));
  Multiplexer #(.Selector_Bits(3)) multiplexer_4 (
    .sel(S), .in_0(C1), .in_1(C2), .in_2(C3), .in_3(C4), .in_4(C5), .in_5(C6), .in_6(C), .in_7(C),
    .out(multiplexer_4_out));
  Add #(.Bits(4)) add_3 (.a(A), .b(4'b0000), .c_i(C), .s(A_plus_C), .c_o(C1));
  Add #(.Bits(4)) add_4 (.a(B), .b(4'b0000), .c_i(C), .s(B_plus_C), .c_o(C6));
  Multiplexer multiplexer_5 (.sel(M), .in_0(C), .in_1(multiplexer_4_out), .out(Cout));
endmodule
