// Digital circuit Template.dig as structural Verilog
module Template (
  input  A,
  input  B,
  input  Cin,
  output Sum1,
  output Cout1,
  output Sum2,
  output Sum3
);

  wire A_t, and_1_out, and_2_out, and_3_out, and_4_out, and_6_out, and_7_out, and_8_out, and_9_out, B_t,
       Cin_t, or_1_out, or_2_out, or_3_out, or_4_out, or_6_out, or_7_out, or_8_out, or_9_out;

  not not_1 (A_t, A);
  not not_2 (B_t, B);
  not not_3 (Cin_t, Cin);
  and and_1 (and_1_out, A_t, B_t, Cin);
  and and_2 (and_2_out, A_t, B, Cin_t);
  and and_3 (and_3_out, A, B_t, Cin_t);
  and and_4 (and_4_out, A, B, Cin);
  or or_1 (or_1_out, A, B, Cin);
  or or_2 (or_2_out, A, B_t, Cin_t);
  or or_3 (or_3_out, A_t, B, Cin_t);
  or or_4 (or_4_out, A_t, B_t, Cin);
  or or_5 (Sum1, and_1_out, and_2_out, and_3_out, and_4_out);
  and and_5 (Sum2, or_1_out, or_2_out, or_3_out, or_4_out);
  and and_6 (and_6_out, A_t, B, Cin);
  and and_7 (and_7_out, A, B_t, Cin);
  and and_8 (and_8_out, A, B, Cin_t);
  and and_9 (and_9_out, A, B, Cin);
  or or_6 (or_6_out, A, B, Cin);
  or or_7 (or_7_out, A, B, Cin_t);
  or or_8 (or_8_out, A, B_t, Cin);
  or or_9 (or_9_out, A_t, B, Cin);
  or or_10 (Cout1, and_6_out, and_7_out, and_8_out, and_9_out);
  and and_10 (Sum3, or_6_out, or_7_out, or_8_out, or_9_out);
endmodule
