// Digital circuit 0506.dig as structural Verilog
module _0506 (
  input  A,
  input  B,
  input  C,
  input  D,
  output Z1,
  output Z2,
  output Z1_2,
  output Z2_2,
  output Z3,
  output Z3_2
);

  wire A_t, and_1_out, and_2_out, and_3_out, and_5_out, and_6_out, and_7_out, and_9_out, and_10_out,
       and_11_out, and_12_out, B_t, C_t, D_t, or_1_out, or_2_out, or_3_out, or_4_out, or_5_out, or_7_out,
       or_8_out, or_9_out, or_10_out, or_11_out, or_13_out, or_14_out, or_15_out, or_16_out;

  not not_1 (A_t, A);
  not not_2 (B_t, B);
  not not_3 (C_t, C);
  not not_4 (D_t, D);
  and and_1 (and_1_out, A, C_t);
  and and_2 (and_2_out, B, C_t, D_t);
  and and_3 (and_3_out, A, B, D_t);
  or or_1 (or_1_out, A, D_t);
  or or_2 (or_2_out, A, B, D);
  or or_3 (or_3_out, A_t, B, C_t);
  or or_4 (or_4_out, A_t, C_t, D_t);
  or or_5 (or_5_out, A, C_t, D);
  or or_6 (Z1, and_1_out, and_2_out, and_3_out);
  and and_4 (Z1_2, or_1_out, or_2_out, or_3_out, or_4_out, or_5_out);
  and and_5 (and_5_out, A_t, C);
  and and_6 (and_6_out, B_t, C, D);
  and and_7 (and_7_out, A_t, B_t, D);
  or or_7 (or_7_out, A_t, D);
  or or_8 (or_8_out, A_t, B_t, D_t);
  or or_9 (or_9_out, A, B_t, C);
  or or_10 (or_10_out, A, C, D);
  or or_11 (or_11_out, A_t, C, D_t);
  or or_12 (Z2, and_5_out, and_6_out, and_7_out);
  and and_8 (Z2_2, or_7_out, or_8_out, or_9_out, or_10_out, or_11_out);
  and and_9 (and_9_out, A, B, C, D);
  and and_10 (and_10_out, A, B_t, C, D_t);
  and and_11 (and_11_out, A_t, B, C_t, D);
  and and_12 (and_12_out, A_t, B_t, C_t, D_t);
  or or_13 (or_13_out, B_t, D);
  or or_14 (or_14_out, B, D_t);
  or or_15 (or_15_out, A, C_t);
  or or_16 (or_16_out, A_t, C);
  or or_17 (Z3, and_9_out, and_10_out, and_11_out, and_12_out);
  and and_13 (Z3_2, or_13_out, or_14_out, or_15_out, or_16_out);
endmodule
