// Digital circuit Template.dig as structural Verilog
module Template (
  input  A,
  input  B,
  input  C,
  input  D,
  output Z1,
  output Z2,
  output Z3,
  output Z1_2,
  output Z2_2,
  output Z3_2
);

  wire A_eq__eq_C, A_gt_C, A_lt_C, A_t, and_3_out, and_4_out, and_5_out, and_6_out, and_7_out, and_8_out,
       and_9_out, and_10_out, B_gt_D, B_lt_D, B_t, C_t, D__eq__eq__B, D_t, or_1_out, or_2_out, or_3_out,
       or_4_out, or_5_out, or_6_out, or_7_out, or_8_out, or_9_out, or_10_out, undriven, undriven_2,
       undriven_3, undriven_4, undriven_5, undriven_6, undriven_7, undriven_8, undriven_9, undriven_10,
       undriven_11, undriven_12;

  and and_1 (A_gt_C, A, C_t);
  xnor xnor_1 (A_eq__eq_C, A, C);
  and and_2 (B_gt_D, B, D_t);
  xnor xnor_2 (D__eq__eq__B, B, D);
  not not_1 (A_t, A);
  not not_2 (B_t, B);
  not not_3 (C_t, C);
  not not_4 (D_t, D);
  nor nor_1 (A_lt_C, A_gt_C, A_eq__eq_C);
  nor nor_2 (B_lt_D, B_gt_D, D__eq__eq__B);
  and and_3 (and_3_out, A, C_t);
  and and_4 (and_4_out, B, C_t, D_t);
  and and_5 (and_5_out, A, B, D_t);
  and and_6 (and_6_out, A_t, C);
  and and_7 (and_7_out, B_t, C, D);
  and and_8 (and_8_out, A_t, B_t, D);
  or or_1 (or_1_out, A_t, D);
  or or_2 (or_2_out, A_t, B_t, D_t);
  or or_3 (or_3_out, A, B_t, C);
  or or_4 (or_4_out, A, C, D);
  or or_5 (or_5_out, A_t, C, D_t);
  or or_6 (or_6_out, A, D_t);
  or or_7 (or_7_out, undriven, undriven_2, undriven_3);
  or or_8 (or_8_out, undriven_4, undriven_5, undriven_6);
  or or_9 (or_9_out, undriven_7, undriven_8, undriven_9);
  or or_10 (or_10_out, undriven_10, undriven_11, undriven_12);
  and and_9 (and_9_out, A_eq__eq_C, B_gt_D);
  and and_10 (and_10_out, B_lt_D, A_eq__eq_C);
  or or_11 (Z1_2, and_3_out, and_4_out, and_5_out);
  or or_12 (Z2_2, and_6_out, and_7_out, and_8_out);
  // And and_11 has open pins: In_1=or_1_out, In_2=or_2_out, In_3=or_3_out, In_4=or_4_out, In_5=or_5_out, out=open
  // And and_12 has open pins: In_1=or_6_out, In_2=or_7_out, In_3=or_8_out, In_4=or_9_out, In_5=or_10_out, out=open
  or or_13 (Z1, A_gt_C, and_9_out);
  or or_14 (Z2, and_10_out, A_lt_C);
  nor nor_3 (Z3, Z1, Z2);
  nor nor_4 (Z3_2, Z1_2, Z2_2);
endmodule
