// Digital circuit Template.dig as structural Verilog
module Template (
  input  X0,
  input  X1,
  input  Selector,
  output Z1,
  output Z2
);

  wire and_1_out, and_2_out, C_t, or_1_out, or_2_out;

  not not_1 (C_t, Selector);
  and and_1 (and_1_out, X0, C_t);
  and and_2 (and_2_out, X1, Selector);
  or or_1 (or_1_out, X0, Selector);
  or or_2 (or_2_out, X1, C_t);
  or or_3 (Z1, and_1_out, and_2_out);
  and and_3 (Z2, or_1_out, or_2_out);

  // Other names for the same wires on the sheet: C = Selector
endmodule
