// Digital circuit 09.dig as structural Verilog
module _09 (
  input  X0,
  input  X1,
  input  S1,
  input  X2,
  input  X3,
  input  S0,
  output Z
);

  wire and_1_out, and_2_out, and_3_out, and_4_out, C_t, D_t;

  not not_1 (C_t, S1);
  not not_2 (D_t, S0);
  and and_1 (and_1_out, X0, C_t, D_t);
  and and_2 (and_2_out, X1, C_t, S0);
  and and_3 (and_3_out, X2, S1, D_t);
  and and_4 (and_4_out, X3, S1, S0);
  or or_1 (Z, and_1_out, and_2_out, and_3_out, and_4_out);

  // Other names for the same wires on the sheet: C = S1; D = S0
endmodule
